// Logisim project Lab2_Problem1.circ as structural Verilog: 1 circuit, main circuit main
module main (
  input  cin,
  input  A,
  input  B,
  output Cout,
  output Cout_2,
  output Sum,
  output Sum_2
);

  wire not_1_out;

  Multiplexer #(.select(2), .enable("false")) multiplexer_1 (
    .in0(1'b0), .in1(B), .in2(B), .in3(A), .out(Cout_2), .sel({cin, B}));
  not not_1 (not_1_out, B);
  Multiplexer #(.select(2), .enable("false")) multiplexer_2 (
    .in0(B), .in1(not_1_out), .in2(not_1_out), .in3(B), .out(Sum_2), .sel({cin, A}));
  Adder #(.width(1)) adder_1 (.a(A), .b(B), .out(Sum), .cin(cin), .cout(Cout));
endmodule
