// Logisim project Lab2_Problem3.circ as structural Verilog: 1 circuit, main circuit main
module main (
  input  reset,
  output [2:0] state
);

  wire bogus_out, clock_1_out, dime_out, nickel_out, priority_encoder_1_gs, quarter_out;
  wire [1:0] priority_encoder_1_out;
  wire [2:0] rom_1_data;

  Button bogus (.out(bogus_out));
  Button nickel (.out(nickel_out));
  Button dime (.out(dime_out));
  Button quarter (.out(quarter_out));
  Priority_Encoder #(.select(2)) priority_encoder_1 (
    .in0(bogus_out), .in1(nickel_out), .in2(dime_out), .in3(quarter_out), .out(priority_encoder_1_out),
    .gs(priority_encoder_1_gs));  // open: en_out, en_in
  // Probe on priority_encoder_1_gs
  ROM #(.addrWidth(5), .dataWidth(3)) rom_1 (.addr({state, priority_encoder_1_out}), .data(rom_1_data));  // open: sel
  Clock clock_1 (.out(clock_1_out));
  Register #(.width(3)) register_1 (.D(rom_1_data), .Q(state), .clk(clock_1_out), .clr(reset));  // open: en

  // Notes on the sheet:
  //   current state
  //   ROM
  //   contents of rom_1 (hex, n*v repeats v):
  //   0 1 2 5 1 2 3 6 2 3 4 6 3 4 5 6 4 5 7*6 1 2 5
  //   next state
  //   clock
  //   Register
endmodule
